// Logisim project SUMLAT.circ as structural Verilog: 1 circuit, main circuit main
module main (
  input  ai,
  input  bi,
  input  ci,
  input  Cin,
  input  Ph,
  input  Gh,
  input  Pl,
  input  Gl,
  output si,
  output pi,
  output gi,
  output PHL,
  output GHL,
  output CH,
  output Cl
);

  wire and_1_out, and_2_out, and_3_out, and_6_out, and_7_out, and_8_out, not_1_out, not_2_out, not_3_out,
       not_4_out, or_4_out;

  and and_1 (and_1_out, Pl, Cin);
  or or_1 (CH, and_1_out, Gl);
  not not_1 (not_1_out, bi);
  not not_2 (not_2_out, ai);
  and and_2 (and_2_out, ai, not_1_out);
  and and_3 (and_3_out, bi, not_2_out);
  and and_4 (PHL, Ph, Pl);
  or or_2 (pi, ai, bi);
  and and_5 (gi, ai, bi);
  and and_6 (and_6_out, Ph, Gl);
  or or_3 (GHL, Gh, and_6_out);
  or or_4 (or_4_out, and_2_out, and_3_out);
  not not_3 (not_3_out, ci);
  not not_4 (not_4_out, or_4_out);
  and and_7 (and_7_out, or_4_out, not_3_out);
  and and_8 (and_8_out, ci, not_4_out);
  or or_5 (si, and_7_out, and_8_out);

  assign Cl = Cin;
endmodule
